// Logisim project cpu-harness.circ as structural Verilog: 1 circuit, main circuit cpu_harness
module cpu_harness (
  input  [31:0] INSTRUCTION,
  input  clk,
  output [31:0] PROGRAM_COUNTER,
  output [31:0] ra,
  output [31:0] sp,
  output [31:0] t0,
  output [31:0] t1,
  output [31:0] t2,
  output [31:0] s0,
  output [31:0] s1,
  output [31:0] a0
);

  wire cpu_1_p3, cpu_1_p4, cpu_1_p14, cpu_1_p15;

  // cpu cpu_1: pin names not known; wires that end beside it: clk, INSTRUCTION, cpu_1_p3, cpu_1_p4, PROGRAM_COUNTER, ra, sp, t0, t1, t2, s0, s1, a0, cpu_1_p14, cpu_1_p15
  // mem mem_1: pin names not known; wires that end beside it: cpu_1_p4, cpu_1_p14, cpu_1_p15, clk, cpu_1_p3

  // Notes on the sheet:
  //   YOUR CPU SHOULD FIT IN HERE!
endmodule
